// Logisim project Using Basic gates.circ as structural Verilog: 1 circuit, main circuit main
module main (
  input  in_1,
  input  in_2
);

  wire and_1_out, and_2_out, and_3_out, and_4_out, and_5_out, and_6_out, and_7_out, and_8_out, and_9_out,
       and_10_out, and_11_out, and_12_out, and_13_out, and_14_out, and_15_out, and_16_out, and_17_out,
       and_18_out, clock_1_out, not_1_out, not_2_out, not_3_out, not_4_out, not_5_out, not_6_out, not_7_out,
       not_8_out, not_9_out, not_10_out, not_11_out, not_12_out, not_13_out, not_14_out, not_15_out,
       not_16_out, not_17_out, or_1_out, or_2_out, or_3_out, or_4_out, or_5_out, or_6_out, or_7_out,
       or_8_out, or_9_out, or_10_out, or_11_out, or_12_out, t_ff_1_q, t_ff_2_q, t_ff_3_q;

  Clock clock_1 (.out(clock_1_out));
  not not_1 (not_1_out, t_ff_2_q);
  not not_2 (not_2_out, t_ff_1_q);
  not not_3 (not_3_out, t_ff_2_q);
  not not_4 (not_4_out, t_ff_2_q);
  not not_5 (not_5_out, t_ff_2_q);
  not not_6 (not_6_out, t_ff_2_q);
  not not_7 (not_7_out, t_ff_1_q);
  not not_8 (not_8_out, t_ff_3_q);
  not not_9 (not_9_out, t_ff_1_q);
  not not_10 (not_10_out, t_ff_3_q);
  not not_11 (not_11_out, t_ff_2_q);
  not not_12 (not_12_out, t_ff_3_q);
  not not_13 (not_13_out, t_ff_1_q);
  not not_14 (not_14_out, t_ff_3_q);
  not not_15 (not_15_out, t_ff_3_q);
  and and_1 (and_1_out, not_1_out, not_2_out);
  and and_2 (and_2_out, t_ff_2_q, t_ff_1_q);
  and and_3 (and_3_out, t_ff_3_q, not_3_out);
  and and_4 (and_4_out, not_4_out, t_ff_1_q);
  and and_5 (and_5_out, t_ff_3_q, not_5_out);
  not not_16 (not_16_out, t_ff_3_q);
  and and_6 (and_6_out, not_6_out, not_7_out);
  and and_7 (and_7_out, not_8_out, not_9_out);
  and and_8 (and_8_out, t_ff_2_q, t_ff_1_q);
  and and_9 (and_9_out, not_10_out, not_11_out);
  and and_10 (and_10_out, not_12_out, not_13_out);
  and and_11 (and_11_out, t_ff_3_q, t_ff_2_q);
  and and_12 (and_12_out, not_14_out, t_ff_1_q);
  not not_17 (not_17_out, t_ff_1_q);
  or or_1 (or_1_out, not_15_out, and_1_out);
  and and_13 (and_13_out, t_ff_2_q, t_ff_1_q);
  or or_2 (or_2_out, and_2_out, and_3_out);
  or or_3 (or_3_out, and_4_out, and_5_out);
  and and_14 (and_14_out, t_ff_3_q, t_ff_1_q);
  or or_4 (or_4_out, not_16_out, and_6_out);
  and and_15 (and_15_out, t_ff_2_q, t_ff_1_q);
  or or_5 (or_5_out, and_7_out, and_8_out);
  or or_6 (or_6_out, and_9_out, and_10_out);
  and and_16 (and_16_out, and_11_out, t_ff_1_q);
  or or_7 (or_7_out, and_12_out, t_ff_2_q);
  and and_17 (and_17_out, t_ff_3_q, not_17_out);
  T_Flip_Flop t_ff_1 (.clk(clock_1_out), .T(in_2), .Q(t_ff_1_q));  // open: Qn, preset, reset, en
  or or_8 (or_8_out, or_1_out, and_13_out);
  or or_9 (or_9_out, or_3_out, and_14_out);
  or or_10 (or_10_out, or_4_out, and_15_out);
  or or_11 (or_11_out, or_6_out, and_16_out);
  or or_12 (or_12_out, or_7_out, and_17_out);
  T_Flip_Flop t_ff_2 (.clk(clock_1_out), .T(t_ff_1_q), .Q(t_ff_2_q));  // open: Qn, preset, reset, en
  and and_18 (and_18_out, t_ff_1_q, t_ff_2_q);
  T_Flip_Flop t_ff_3 (.clk(clock_1_out), .T(and_18_out), .Q(t_ff_3_q));  // open: Qn, preset, reset, en
  _7_Segment_Display u_7_segment_display_1 (
    .g(or_12_out), .f(or_11_out), .a(or_8_out), .b(or_2_out), .e(or_5_out), .d(or_10_out), .c(or_9_out),
    .dp(in_1));
endmodule
