// Logisim project Using Decoder .circ as structural Verilog
module _3_to_8_Decoder (
  input  A,
  input  B,
  input  C
);

  wire and_1_out, and_2_out, and_3_out, and_4_out, and_5_out, and_6_out, and_7_out, and_8_out, and_9_out,
       and_10_out, and_11_out, and_12_out, and_13_out, and_14_out, and_15_out, and_16_out, not_1_out,
       not_2_out, not_3_out, not_4_out, not_5_out, not_6_out, not_7_out, not_8_out, not_9_out, not_10_out,
       not_11_out, not_12_out, or_1_out, or_2_out, or_3_out, or_4_out, or_5_out, or_6_out, or_7_out;

  not not_1 (not_1_out, A);
  not not_2 (not_2_out, B);
  not not_3 (not_3_out, A);
  not not_4 (not_4_out, B);
  not not_5 (not_5_out, A);
  not not_6 (not_6_out, A);
  not not_7 (not_7_out, B);
  not not_8 (not_8_out, B);
  and and_1 (and_1_out, A, B);
  not not_9 (not_9_out, C);
  and and_2 (and_2_out, A, B);
  and and_3 (and_3_out, not_1_out, not_2_out);
  not not_10 (not_10_out, C);
  and and_4 (and_4_out, not_3_out, not_4_out);
  and and_5 (and_5_out, not_5_out, B);
  not not_11 (not_11_out, C);
  and and_6 (and_6_out, not_6_out, B);
  and and_7 (and_7_out, A, not_7_out);
  not not_12 (not_12_out, C);
  and and_8 (and_8_out, A, not_8_out);
  and and_9 (and_9_out, and_1_out, not_9_out);
  and and_10 (and_10_out, and_2_out, C);
  and and_11 (and_11_out, and_3_out, not_10_out);
  and and_12 (and_12_out, and_4_out, C);
  and and_13 (and_13_out, and_5_out, not_11_out);
  and and_14 (and_14_out, and_6_out, C);
  and and_15 (and_15_out, and_7_out, not_12_out);
  and and_16 (and_16_out, and_8_out, C);
  or or_1 (or_1_out, and_11_out, and_12_out, and_13_out, and_14_out, and_15_out, and_10_out);
  or or_2 (or_2_out, and_14_out, and_15_out, and_16_out, and_10_out);
  or or_3 (or_3_out, and_11_out, and_12_out, and_13_out, and_14_out, and_15_out, and_10_out);
  or or_4 (or_4_out, and_12_out, and_15_out, and_16_out, and_10_out);
  _7_Segment_Display u_7_segment_display_1 (
    .g(or_7_out), .f(or_6_out), .a(or_1_out), .b(or_2_out), .e(or_5_out), .d(or_3_out), .c(or_4_out));  // open: dp
  or or_5 (or_5_out, and_11_out, and_13_out, and_14_out, and_10_out);
  or or_6 (or_6_out, and_11_out, and_12_out, and_13_out, and_10_out);
  or or_7 (or_7_out, and_12_out, and_13_out, and_14_out, and_15_out, and_9_out, and_10_out);

  // Notes on the sheet:
  //   0
  //   1
  //   2
  //   3
  //   4
  //   5
  //   6
  //   7
  //   a
  //   b
  //   c
  //   d
  //   e
  //   f
  //   g
endmodule
