// Logisim project Using MUX.circ as structural Verilog: 1 circuit, main circuit main
module main (
  input  Ground,
  input  Power,
  input  C_prime,
  input  [1:0] A____B
);

  wire multiplexer_1_out, multiplexer_2_out, multiplexer_3_out, multiplexer_4_out, multiplexer_5_out,
       multiplexer_6_out, multiplexer_7_out, not_1_out;

  not not_1 (not_1_out, C_prime);
  Multiplexer #(.select(2), .enable("false")) multiplexer_1 (
    .in0(Power), .in1(Power), .in2(not_1_out), .in3(C_prime), .out(multiplexer_1_out), .sel(A____B));
  Multiplexer #(.select(2), .enable("false")) multiplexer_2 (
    .in0(Ground), .in1(C_prime), .in2(Power), .in3(C_prime), .out(multiplexer_2_out), .sel(A____B));
  Multiplexer #(.select(2), .enable("false")) multiplexer_3 (
    .in0(C_prime), .in1(Ground), .in2(Power), .in3(C_prime), .out(multiplexer_3_out), .sel(A____B));
  Multiplexer #(.select(2), .enable("false")) multiplexer_4 (
    .in0(Power), .in1(Power), .in2(not_1_out), .in3(C_prime), .out(multiplexer_4_out), .sel(A____B));
  Multiplexer #(.select(2), .enable("false")) multiplexer_5 (
    .in0(not_1_out), .in1(Power), .in2(Ground), .in3(C_prime), .out(multiplexer_5_out), .sel(A____B));
  Multiplexer #(.select(2), .enable("false")) multiplexer_6 (
    .in0(Power), .in1(not_1_out), .in2(Ground), .in3(C_prime), .out(multiplexer_6_out), .sel(A____B));
  Multiplexer #(.select(2), .enable("false")) multiplexer_7 (
    .in0(C_prime), .in1(Power), .in2(not_1_out), .in3(Power), .out(multiplexer_7_out), .sel(A____B));
  _7_Segment_Display u_7_segment_display_1 (
    .g(multiplexer_7_out), .f(multiplexer_6_out), .a(multiplexer_1_out), .b(multiplexer_2_out),
    .e(multiplexer_5_out), .d(multiplexer_4_out), .c(multiplexer_3_out));  // open: dp

  // Notes on the sheet:
  //   C
  //   a
  //   b
  //   c
  //   d
  //   e
  //   f
  //   g
endmodule
